// Logisim project CPU_v2.circ as structural Verilog: 10 circuits, main circuit main
module main (
);

  wire bcd_7seg_1_a, bcd_7seg_1_b, bcd_7seg_1_c, bcd_7seg_1_d, bcd_7seg_1_decimal, bcd_7seg_1_e,
       bcd_7seg_1_f, bcd_7seg_1_g, bcd_7seg_2_a, bcd_7seg_2_b, bcd_7seg_2_c, bcd_7seg_2_d,
       bcd_7seg_2_decimal, bcd_7seg_2_e, bcd_7seg_2_f, bcd_7seg_2_g, bcd_7seg_3_a, bcd_7seg_3_b,
       bcd_7seg_3_c, bcd_7seg_3_d, bcd_7seg_3_decimal, bcd_7seg_3_e, bcd_7seg_3_f, bcd_7seg_3_g,
       bcd_7seg_4_a, bcd_7seg_4_b, bcd_7seg_4_c, bcd_7seg_4_d, bcd_7seg_4_decimal, bcd_7seg_4_e,
       bcd_7seg_4_f, bcd_7seg_4_g, bcd_7seg_5_a, bcd_7seg_5_b, bcd_7seg_5_c, bcd_7seg_5_d,
       bcd_7seg_5_decimal, bcd_7seg_5_e, bcd_7seg_5_f, bcd_7seg_5_g, bcd_7seg_6_a, bcd_7seg_6_b,
       bcd_7seg_6_c, bcd_7seg_6_d, bcd_7seg_6_decimal, bcd_7seg_6_e, bcd_7seg_6_f, bcd_7seg_6_g,
       bcd_7seg_7_a, bcd_7seg_7_b, bcd_7seg_7_c, bcd_7seg_7_d, bcd_7seg_7_decimal, bcd_7seg_7_e,
       bcd_7seg_7_f, bcd_7seg_7_g, bcd_7seg_8_a, bcd_7seg_8_b, bcd_7seg_8_c, bcd_7seg_8_d,
       bcd_7seg_8_decimal, bcd_7seg_8_e, bcd_7seg_8_f, bcd_7seg_8_g, bcd_7seg_9_a, bcd_7seg_9_b,
       bcd_7seg_9_c, bcd_7seg_9_d, bcd_7seg_9_decimal, bcd_7seg_9_e, bcd_7seg_9_f, bcd_7seg_9_g,
       bcd_7seg_10_a, bcd_7seg_10_b, bcd_7seg_10_c, bcd_7seg_10_d, bcd_7seg_10_decimal, bcd_7seg_10_e,
       bcd_7seg_10_f, bcd_7seg_10_g, bcd_7seg_11_a, bcd_7seg_11_b, bcd_7seg_11_c, bcd_7seg_11_d,
       bcd_7seg_11_decimal, bcd_7seg_11_e, bcd_7seg_11_f, bcd_7seg_11_g, bcd_7seg_12_a, bcd_7seg_12_b,
       bcd_7seg_12_c, bcd_7seg_12_d, bcd_7seg_12_decimal, bcd_7seg_12_e, bcd_7seg_12_f, bcd_7seg_12_g,
       clock_1_out, clock_2_out, clock_3_out, clock_4_out, clock_5_out, clock_6_out, d_ff_1_q, d_ff_2_q,
       en_write, not_1_out, not_2_out, not_3_out, op2_is_imm, por_1_out, R, ram_in, ram_ope, small_rd,
       writeback_alu;
  wire [1:0] ldiCode, PcMode;
  wire [3:0] bin_to_bcd_1_bcd1, bin_to_bcd_1_bcd10, bin_to_bcd_1_bcd100, bin_to_bcd_2_bcd1,
       bin_to_bcd_2_bcd10, bin_to_bcd_2_bcd100, bin_to_bcd_3_bcd1, bin_to_bcd_3_bcd10, bin_to_bcd_3_bcd100,
       bin_to_bcd_4_bcd1, bin_to_bcd_4_bcd10, bin_to_bcd_4_bcd100, RA2, WA_RA1;
  wire [4:0] AluOp;
  wire [7:0] ALU_Result, Immediate, R0, R1, R2, R3, R4, R5, R6, ram_1_dout, RD1, RD2, RD2_out, RD3,
       RegFileInput;
  wire [15:0] PcReg, romdata_1_romout;

  POR por_1 (.out(por_1_out));
  Clock clock_1 (.out(clock_1_out));
  // Probe on R0
  // Probe on R1
  // Probe on R2
  // Probe on R3
  // Probe on R4
  // Probe on R5
  // Probe on R6
  // Probe on {R1, R0}
  // Probe on {R3, R2}
  // Probe on {R5, R4}
  // Probe on {R2, R1, R0}
  // Probe on {R5, R4, R3}
  D_Flip_Flop d_ff_1 (.D(por_1_out), .clk(clock_1_out), .Q(d_ff_1_q), .preset(por_1_out));  // open: Qn, reset
  // Probe on nothing
  D_Flip_Flop d_ff_2 (.D(d_ff_1_q), .clk(clock_1_out), .Q(d_ff_2_q), .preset(por_1_out));  // open: Qn, reset
  // Probe on R0
  // Probe on R1
  // Probe on R2
  // Probe on R3
  // Probe on R4
  // Probe on R5
  // Probe on R6
  // Probe on {R1, R0}
  // Probe on {R3, R2}
  // Probe on {R5, R4}
  D_Flip_Flop d_ff_3 (.D(d_ff_2_q), .clk(clock_1_out), .Q(R), .preset(por_1_out));  // open: Qn, reset
  // Probe on {R2, R1, R0}
  // Probe on {R5, R4, R3}
  assign RD2_out = not_1_out ? RD2 : 8'bz;  // Controlled_Buffer controlled_buffer_1
  not not_1 (not_1_out, op2_is_imm);
  assign RD2_out = op2_is_imm ? Immediate : 8'bz;  // Controlled_Buffer controlled_buffer_2
  _7_Segment_Display u_7_segment_display_1 (
    .g(bcd_7seg_1_g), .f(bcd_7seg_1_f), .a(bcd_7seg_1_a), .b(bcd_7seg_1_b), .e(bcd_7seg_1_e),
    .d(bcd_7seg_1_d), .c(bcd_7seg_1_c), .dp(bcd_7seg_1_decimal));
  bcd_7seg bcd_7seg_1 (
    .bcd(bin_to_bcd_1_bcd100), .b(bcd_7seg_1_b), .c(bcd_7seg_1_c), .d(bcd_7seg_1_d), .e(bcd_7seg_1_e),
    .f(bcd_7seg_1_f), .g(bcd_7seg_1_g), .decimal(bcd_7seg_1_decimal), .a(bcd_7seg_1_a));
  bin_to_bcd bin_to_bcd_1 (
    .in_1(RegFileInput), .bcd100(bin_to_bcd_1_bcd100), .bcd10(bin_to_bcd_1_bcd10), .bcd1(bin_to_bcd_1_bcd1));
  LedBar ledbar_1 (
    .led0(RegFileInput[7]), .led1(RegFileInput[6]), .led2(RegFileInput[5]), .led3(RegFileInput[4]),
    .led4(RegFileInput[3]), .led5(RegFileInput[2]), .led6(RegFileInput[1]), .led7(RegFileInput[0]));
  assign RegFileInput = not_2_out ? RD2_out : 8'bz;  // Controlled_Buffer controlled_buffer_3
  not not_2 (not_2_out, writeback_alu);
  assign RegFileInput = writeback_alu ? ALU_Result : 8'bz;  // Controlled_Buffer controlled_buffer_4
  Clock clock_2 (.out(clock_2_out));
  _7_Segment_Display u_7_segment_display_2 (
    .g(bcd_7seg_2_g), .f(bcd_7seg_2_f), .a(bcd_7seg_2_a), .b(bcd_7seg_2_b), .e(bcd_7seg_2_e),
    .d(bcd_7seg_2_d), .c(bcd_7seg_2_c), .dp(bcd_7seg_2_decimal));
  _7_Segment_Display u_7_segment_display_3 (
    .g(bcd_7seg_3_g), .f(bcd_7seg_3_f), .a(bcd_7seg_3_a), .b(bcd_7seg_3_b), .e(bcd_7seg_3_e),
    .d(bcd_7seg_3_d), .c(bcd_7seg_3_c), .dp(bcd_7seg_3_decimal));
  bcd_7seg bcd_7seg_2 (
    .bcd(bin_to_bcd_1_bcd1), .b(bcd_7seg_2_b), .c(bcd_7seg_2_c), .d(bcd_7seg_2_d), .e(bcd_7seg_2_e),
    .f(bcd_7seg_2_f), .g(bcd_7seg_2_g), .decimal(bcd_7seg_2_decimal), .a(bcd_7seg_2_a));
  bcd_7seg bcd_7seg_3 (
    .bcd(bin_to_bcd_1_bcd10), .b(bcd_7seg_3_b), .c(bcd_7seg_3_c), .d(bcd_7seg_3_d), .e(bcd_7seg_3_e),
    .f(bcd_7seg_3_f), .g(bcd_7seg_3_g), .decimal(bcd_7seg_3_decimal), .a(bcd_7seg_3_a));
  Clock clock_3 (.out(clock_3_out));
  Clock clock_4 (.out(clock_4_out));
  Clock clock_5 (.out(clock_5_out));
  Clock clock_6 (.out(clock_6_out));
  _7_Segment_Display u_7_segment_display_4 (
    .g(bcd_7seg_4_g), .f(bcd_7seg_4_f), .a(bcd_7seg_4_a), .b(bcd_7seg_4_b), .e(bcd_7seg_4_e),
    .d(bcd_7seg_4_d), .c(bcd_7seg_4_c), .dp(bcd_7seg_4_decimal));
  bcd_7seg bcd_7seg_4 (
    .bcd(bin_to_bcd_2_bcd100), .b(bcd_7seg_4_b), .c(bcd_7seg_4_c), .d(bcd_7seg_4_d), .e(bcd_7seg_4_e),
    .f(bcd_7seg_4_f), .g(bcd_7seg_4_g), .decimal(bcd_7seg_4_decimal), .a(bcd_7seg_4_a));
  bin_to_bcd bin_to_bcd_2 (
    .in_1(RD1), .bcd100(bin_to_bcd_2_bcd100), .bcd10(bin_to_bcd_2_bcd10), .bcd1(bin_to_bcd_2_bcd1));
  RAM #(.addrWidth(16), .enables("line")) ram_1 (
    .addr({RD3, RD2}), .we(ram_in), .clk(clock_6_out), .din(RD1), .dout(ram_1_dout));
  _7_Segment_Display u_7_segment_display_5 (
    .g(bcd_7seg_5_g), .f(bcd_7seg_5_f), .a(bcd_7seg_5_a), .b(bcd_7seg_5_b), .e(bcd_7seg_5_e),
    .d(bcd_7seg_5_d), .c(bcd_7seg_5_c), .dp(bcd_7seg_5_decimal));
  bcd_7seg bcd_7seg_5 (
    .bcd(bin_to_bcd_2_bcd10), .b(bcd_7seg_5_b), .c(bcd_7seg_5_c), .d(bcd_7seg_5_d), .e(bcd_7seg_5_e),
    .f(bcd_7seg_5_f), .g(bcd_7seg_5_g), .decimal(bcd_7seg_5_decimal), .a(bcd_7seg_5_a));
  LedBar ledbar_2 (
    .led0(RD1[7]), .led1(RD1[6]), .led2(RD1[5]), .led3(RD1[4]), .led4(RD1[3]), .led5(RD1[2]), .led6(RD1[1]),
    .led7(RD1[0]));
  _7_Segment_Display u_7_segment_display_6 (
    .g(bcd_7seg_6_g), .f(bcd_7seg_6_f), .a(bcd_7seg_6_a), .b(bcd_7seg_6_b), .e(bcd_7seg_6_e),
    .d(bcd_7seg_6_d), .c(bcd_7seg_6_c), .dp(bcd_7seg_6_decimal));
  _7_Segment_Display u_7_segment_display_7 (
    .g(bcd_7seg_7_g), .f(bcd_7seg_7_f), .a(bcd_7seg_7_a), .b(bcd_7seg_7_b), .e(bcd_7seg_7_e),
    .d(bcd_7seg_7_d), .c(bcd_7seg_7_c), .dp(bcd_7seg_7_decimal));
  bcd_7seg bcd_7seg_6 (
    .bcd(bin_to_bcd_2_bcd1), .b(bcd_7seg_6_b), .c(bcd_7seg_6_c), .d(bcd_7seg_6_d), .e(bcd_7seg_6_e),
    .f(bcd_7seg_6_f), .g(bcd_7seg_6_g), .decimal(bcd_7seg_6_decimal), .a(bcd_7seg_6_a));
  bcd_7seg bcd_7seg_7 (
    .bcd(bin_to_bcd_3_bcd100), .b(bcd_7seg_7_b), .c(bcd_7seg_7_c), .d(bcd_7seg_7_d), .e(bcd_7seg_7_e),
    .f(bcd_7seg_7_f), .g(bcd_7seg_7_g), .decimal(bcd_7seg_7_decimal), .a(bcd_7seg_7_a));
  bin_to_bcd bin_to_bcd_3 (
    .in_1(RD2_out), .bcd100(bin_to_bcd_3_bcd100), .bcd10(bin_to_bcd_3_bcd10), .bcd1(bin_to_bcd_3_bcd1));
  RegisterFile registerfile_1 (
    .EnableWrite(en_write), .Write(WA_RA1[2:0]), .WriteData(RegFileInput), .PortA(WA_RA1[2:0]),
    .PortB(RA2[2:0]), .clk(clock_3_out), .RD1(RD1), .RD2(RD2), .RD3(RD3), .R6_out(R6), .R5_out(R5),
    .R4_out(R4), .R3_out(R3), .R2_out(R2), .R1_out(R1), .R0_out(R0));
  ALU alu_1 (.AluOp(AluOp), .Enable(writeback_alu), .RD1(RD1), .RD2(RD2), .clk(clock_4_out), .Result(ALU_Result));
  RomData romdata_1 (
    .PC(PcReg), .clk(clock_5_out), .NotEnable(ram_ope),
    .RomOut({romdata_1_romout[15:14], RA2, romdata_1_romout[9:8], WA_RA1[1:0], romdata_1_romout[5:0]}));
  ProgramCounter programcounter_1 (
    .RelativeAddr(RD2_out), .AbisoluteAddr({RD3, RD2}), .CounterMode(PcMode), .clk(clock_2_out), .Reset(R),
    .PC(PcReg));
  _7_Segment_Display u_7_segment_display_8 (
    .g(bcd_7seg_8_g), .f(bcd_7seg_8_f), .a(bcd_7seg_8_a), .b(bcd_7seg_8_b), .e(bcd_7seg_8_e),
    .d(bcd_7seg_8_d), .c(bcd_7seg_8_c), .dp(bcd_7seg_8_decimal));
  bcd_7seg bcd_7seg_8 (
    .bcd(bin_to_bcd_3_bcd10), .b(bcd_7seg_8_b), .c(bcd_7seg_8_c), .d(bcd_7seg_8_d), .e(bcd_7seg_8_e),
    .f(bcd_7seg_8_f), .g(bcd_7seg_8_g), .decimal(bcd_7seg_8_decimal), .a(bcd_7seg_8_a));
  LedBar ledbar_3 (
    .led0(RD2_out[7]), .led1(RD2_out[6]), .led2(RD2_out[5]), .led3(RD2_out[4]), .led4(RD2_out[3]),
    .led5(RD2_out[2]), .led6(RD2_out[1]), .led7(RD2_out[0]));
  _7_Segment_Display u_7_segment_display_9 (
    .g(bcd_7seg_9_g), .f(bcd_7seg_9_f), .a(bcd_7seg_9_a), .b(bcd_7seg_9_b), .e(bcd_7seg_9_e),
    .d(bcd_7seg_9_d), .c(bcd_7seg_9_c), .dp(bcd_7seg_9_decimal));
  _7_Segment_Display u_7_segment_display_10 (
    .g(bcd_7seg_10_g), .f(bcd_7seg_10_f), .a(bcd_7seg_10_a), .b(bcd_7seg_10_b), .e(bcd_7seg_10_e),
    .d(bcd_7seg_10_d), .c(bcd_7seg_10_c), .dp(bcd_7seg_10_decimal));
  bcd_7seg bcd_7seg_9 (
    .bcd(bin_to_bcd_3_bcd1), .b(bcd_7seg_9_b), .c(bcd_7seg_9_c), .d(bcd_7seg_9_d), .e(bcd_7seg_9_e),
    .f(bcd_7seg_9_f), .g(bcd_7seg_9_g), .decimal(bcd_7seg_9_decimal), .a(bcd_7seg_9_a));
  bcd_7seg bcd_7seg_10 (
    .bcd(bin_to_bcd_4_bcd100), .b(bcd_7seg_10_b), .c(bcd_7seg_10_c), .d(bcd_7seg_10_d), .e(bcd_7seg_10_e),
    .f(bcd_7seg_10_f), .g(bcd_7seg_10_g), .decimal(bcd_7seg_10_decimal), .a(bcd_7seg_10_a));
  bin_to_bcd bin_to_bcd_4 (
    .in_1(RD3), .bcd100(bin_to_bcd_4_bcd100), .bcd10(bin_to_bcd_4_bcd10), .bcd1(bin_to_bcd_4_bcd1));
  not not_3 (not_3_out, ram_ope);
  _7_Segment_Display u_7_segment_display_11 (
    .g(bcd_7seg_11_g), .f(bcd_7seg_11_f), .a(bcd_7seg_11_a), .b(bcd_7seg_11_b), .e(bcd_7seg_11_e),
    .d(bcd_7seg_11_d), .c(bcd_7seg_11_c), .dp(bcd_7seg_11_decimal));
  bcd_7seg bcd_7seg_11 (
    .bcd(bin_to_bcd_4_bcd10), .b(bcd_7seg_11_b), .c(bcd_7seg_11_c), .d(bcd_7seg_11_d), .e(bcd_7seg_11_e),
    .f(bcd_7seg_11_f), .g(bcd_7seg_11_g), .decimal(bcd_7seg_11_decimal), .a(bcd_7seg_11_a));
  LedBar ledbar_4 (
    .led0(RD3[7]), .led1(RD3[6]), .led2(RD3[5]), .led3(RD3[4]), .led4(RD3[3]), .led5(RD3[2]), .led6(RD3[1]),
    .led7(RD3[0]));
  assign Immediate = not_3_out ? {romdata_1_romout[15:14], RA2, romdata_1_romout[9:8]} : 8'bz;  // Controlled_Buffer controlled_buffer_5
  assign Immediate = ram_ope ? ram_1_dout : 8'bz;  // Controlled_Buffer controlled_buffer_6
  _7_Segment_Display u_7_segment_display_12 (
    .g(bcd_7seg_12_g), .f(bcd_7seg_12_f), .a(bcd_7seg_12_a), .b(bcd_7seg_12_b), .e(bcd_7seg_12_e),
    .d(bcd_7seg_12_d), .c(bcd_7seg_12_c), .dp(bcd_7seg_12_decimal));
  bcd_7seg bcd_7seg_12 (
    .bcd(bin_to_bcd_4_bcd1), .b(bcd_7seg_12_b), .c(bcd_7seg_12_c), .d(bcd_7seg_12_d), .e(bcd_7seg_12_e),
    .f(bcd_7seg_12_f), .g(bcd_7seg_12_g), .decimal(bcd_7seg_12_decimal), .a(bcd_7seg_12_a));
  Multiplexer #(.width(2)) multiplexer_1 (
    .in0(romdata_1_romout[9:8]), .in1(ldiCode), .out(WA_RA1[3:2]), .sel(small_rd));
  InstructionDecoder instructiondecoder_1 (
    .opcode(romdata_1_romout[5:0]), .CounterMode(PcMode), .writeback_alu(writeback_alu),
    .op2_is_imm(op2_is_imm), .en_write_reg1(en_write), .small_rd(small_rd), .LdiCode(ldiCode),
    .Ram_out(ram_ope), .Ram_In(ram_in), .AluOp(AluOp));

  // Other names for the same wires on the sheet: RD32[15:0] = {RD3, RD2}
endmodule

module AluDecoder (
  input  [4:0] F,
  input  CondMatch,
  output [1:0] COp,
  output [1:0] SOp,
  output [3:0] InvRHS
);

  wire and_1_out, and_2_out, and_3_out, and_4_out, and_5_out, and_6_out, and_7_out, and_8_out, and_10_out,
       and_11_out, and_12_out, and_13_out, and_14_out, and_15_out, and_16_out, and_17_out, and_18_out,
       and_19_out, and_20_out, and_21_out, and_22_out, and_23_out, not_1_out, not_2_out, not_3_out,
       not_4_out, not_5_out, not_6_out;

  not not_1 (not_1_out, F[4]);
  not not_2 (not_2_out, F[3]);
  not not_3 (not_3_out, F[2]);
  not not_4 (not_4_out, F[1]);
  not not_5 (not_5_out, F[0]);
  not not_6 (not_6_out, CondMatch);
  and and_1 (and_1_out, not_1_out, not_3_out, F[0]);
  and and_2 (and_2_out, not_1_out, not_2_out, F[1], F[0]);
  and and_3 (and_3_out, not_1_out, F[3], not_3_out, F[1]);
  and and_4 (and_4_out, not_1_out, not_2_out, not_3_out, F[1]);
  and and_5 (and_5_out, not_1_out, not_2_out, F[0]);
  and and_6 (and_6_out, not_1_out, not_3_out, F[0]);
  and and_7 (and_7_out, not_1_out, not_2_out, F[2], F[1]);
  and and_8 (and_8_out, not_1_out, F[3], not_3_out);
  and and_9 (SOp[0], not_1_out, not_3_out);
  and and_10 (and_10_out, not_2_out, not_3_out, not_4_out);
  and and_11 (and_11_out, F[3], F[2], not_4_out);
  and and_12 (and_12_out, F[3], F[2], not_5_out);
  and and_13 (and_13_out, not_1_out, not_2_out, not_3_out, F[1]);
  and and_14 (and_14_out, not_1_out, F[3], F[2], not_5_out);
  and and_15 (and_15_out, F[4], not_6_out);
  and and_16 (and_16_out, not_1_out, F[3], F[1], F[0]);
  and and_17 (and_17_out, not_1_out, not_2_out, not_4_out);
  and and_18 (and_18_out, F[4], CondMatch);
  and and_19 (and_19_out, not_1_out, F[3], F[2], not_5_out);
  and and_20 (and_20_out, not_1_out, F[3], F[2], F[1]);
  and and_21 (and_21_out, not_1_out, not_2_out, not_3_out, F[1]);
  and and_22 (and_22_out, not_1_out, F[2], not_4_out, not_5_out);
  and and_23 (and_23_out, not_1_out, not_2_out, F[2], not_4_out);
  or or_1 (COp[1], and_1_out, and_2_out, and_3_out);
  or or_2 (COp[0], and_4_out, and_5_out, and_6_out);
  or or_3 (SOp[1], and_7_out, and_8_out);
  or or_4 (InvRHS[3], and_10_out, and_11_out, and_12_out, F[4]);
  or or_5 (InvRHS[2], and_13_out, and_14_out, and_15_out, and_16_out);
  or or_6 (InvRHS[1], and_17_out, and_18_out, and_19_out, and_20_out);
  or or_7 (InvRHS[0], and_21_out, and_22_out, and_23_out);
endmodule

module PLA_Decoder_LOp (
  input  [3:0] LOp,
  input  [3:0] RD2,
  input  [3:0] RD1,
  output Swap,
  output [3:0] result
);

  PLA #(.in_width(12), .out_width(1), .\table ("xxxxxxxx1111 1")) pla_1 (.in({RD1, RD2, LOp}), .out(Swap));
  PLA #(.in_width(12), .out_width(1), .\table ("xxx0xxx0xxx1 1\nxxx0xxx1xx1x 1\nxxx1xxx0x1xx 1\nxxx1xxx11xxx 1")) pla_2 (
    .in({RD1, RD2, LOp}), .out(result[0]));
  PLA #(.in_width(12), .out_width(1), .\table ("xx0xxx0xxxx1 1\nxx0xxx1xxx1x 1\nxx1xxx0xx1xx 1\nxx1xxx1x1xxx 1")) pla_3 (
    .in({RD1, RD2, LOp}), .out(result[1]));
  PLA #(.in_width(12), .out_width(1), .\table ("x0xxx0xxxxx1 1\nx0xxx1xxxx1x 1\nx1xxx0xxx1xx 1\nx1xxx1xx1xxx 1")) pla_4 (
    .in({RD1, RD2, LOp}), .out(result[2]));
  PLA #(.in_width(12), .out_width(1), .\table ("0xxx0xxxxxx1 1\n0xxx1xxxxx1x 1\n1xxx0xxxx1xx 1\n1xxx1xxx1xxx 1")) pla_5 (
    .in({RD1, RD2, LOp}), .out(result[3]));
endmodule

module RegisterFile (
  input  EnableWrite,
  input  [2:0] Write,
  input  [7:0] WriteData,
  input  [2:0] PortA,
  input  [2:0] PortB,
  input  clk,
  output [7:0] RD1,
  output [7:0] RD2,
  output [7:0] RD3,
  output [7:0] R6_out,
  output [7:0] R5_out,
  output [7:0] R4_out,
  output [7:0] R3_out,
  output [7:0] R2_out,
  output [7:0] R1_out,
  output [7:0] R0_out
);

  wire decoder_1_out1, decoder_1_out2, decoder_1_out3, decoder_1_out4, decoder_1_out5, decoder_1_out6,
       decoder_1_out7, decoder_2_out0, decoder_2_out1, decoder_2_out2, decoder_2_out3, decoder_2_out4,
       decoder_2_out5, decoder_2_out6, decoder_2_out7, decoder_3_out0, decoder_3_out1, decoder_3_out2,
       decoder_3_out3, decoder_3_out4, decoder_3_out5, decoder_3_out6, decoder_3_out7;

  Decoder #(.select(3)) decoder_1 (
    .out1(decoder_1_out1), .out2(decoder_1_out2), .out3(decoder_1_out3), .out4(decoder_1_out4),
    .out5(decoder_1_out5), .out6(decoder_1_out6), .out7(decoder_1_out7), .sel(Write), .en(EnableWrite));  // open: out0
  LedBar ledbar_1 (
    .led0(WriteData[7]), .led1(WriteData[6]), .led2(WriteData[5]), .led3(WriteData[4]), .led4(WriteData[3]),
    .led5(WriteData[2]), .led6(WriteData[1]), .led7(WriteData[0]));
  Register R6 (.D(WriteData), .en(decoder_1_out7), .clk(clk), .Q(R6_out));  // open: clr
  Register R5 (.D(WriteData), .en(decoder_1_out6), .clk(clk), .Q(R5_out));  // open: clr
  Register R4 (.D(WriteData), .en(decoder_1_out5), .clk(clk), .Q(R4_out));  // open: clr
  Register R3 (.D(WriteData), .en(decoder_1_out4), .clk(clk), .Q(R3_out));  // open: clr
  Register R2 (.D(WriteData), .en(decoder_1_out3), .clk(clk), .Q(R2_out));  // open: clr
  Register R1 (.D(WriteData), .en(decoder_1_out2), .clk(clk), .Q(R1_out));  // open: clr
  Register R0 (.D(WriteData), .en(decoder_1_out1), .clk(clk), .Q(R0_out));  // open: clr
  Decoder #(.enable("false"), .select(3)) decoder_2 (
    .out0(decoder_2_out0), .out1(decoder_2_out1), .out2(decoder_2_out2), .out3(decoder_2_out3),
    .out4(decoder_2_out4), .out5(decoder_2_out5), .out6(decoder_2_out6), .out7(decoder_2_out7), .sel(PortA));
  assign RD1 = decoder_2_out6 ? R5_out : 8'bz;  // Controlled_Buffer controlled_buffer_1
  assign RD1 = decoder_2_out5 ? R4_out : 8'bz;  // Controlled_Buffer controlled_buffer_2
  assign RD1 = decoder_2_out3 ? R2_out : 8'bz;  // Controlled_Buffer controlled_buffer_3
  assign RD1 = decoder_2_out2 ? R1_out : 8'bz;  // Controlled_Buffer controlled_buffer_4
  Decoder #(.enable("false"), .select(3)) decoder_3 (
    .out0(decoder_3_out0), .out1(decoder_3_out1), .out2(decoder_3_out2), .out3(decoder_3_out3),
    .out4(decoder_3_out4), .out5(decoder_3_out5), .out6(decoder_3_out6), .out7(decoder_3_out7), .sel(PortB));
  assign RD1 = decoder_2_out7 ? R6_out : 8'bz;  // Controlled_Buffer controlled_buffer_5
  assign RD1 = decoder_2_out4 ? R3_out : 8'bz;  // Controlled_Buffer controlled_buffer_6
  assign RD1 = decoder_2_out1 ? R0_out : 8'bz;  // Controlled_Buffer controlled_buffer_7
  assign RD1 = decoder_2_out0 ? {8{1'b0}} : 8'bz;  // Controlled_Buffer controlled_buffer_8
  LedBar ledbar_2 (
    .led0(RD1[7]), .led1(RD1[6]), .led2(RD1[5]), .led3(RD1[4]), .led4(RD1[3]), .led5(RD1[2]), .led6(RD1[1]),
    .led7(RD1[0]));
  assign RD2 = decoder_3_out7 ? R6_out : 8'bz;  // Controlled_Buffer controlled_buffer_9
  assign RD2 = decoder_3_out6 ? R5_out : 8'bz;  // Controlled_Buffer controlled_buffer_10
  assign RD2 = decoder_3_out5 ? R4_out : 8'bz;  // Controlled_Buffer controlled_buffer_11
  assign RD2 = decoder_3_out4 ? R3_out : 8'bz;  // Controlled_Buffer controlled_buffer_12
  assign RD2 = decoder_3_out3 ? R2_out : 8'bz;  // Controlled_Buffer controlled_buffer_13
  assign RD2 = decoder_3_out2 ? R1_out : 8'bz;  // Controlled_Buffer controlled_buffer_14
  assign RD2 = decoder_3_out1 ? R0_out : 8'bz;  // Controlled_Buffer controlled_buffer_15
  assign RD2 = decoder_3_out0 ? {8{1'b0}} : 8'bz;  // Controlled_Buffer controlled_buffer_16
  LedBar ledbar_3 (
    .led0(RD2[7]), .led1(RD2[6]), .led2(RD2[5]), .led3(RD2[4]), .led4(RD2[3]), .led5(RD2[2]), .led6(RD2[1]),
    .led7(RD2[0]));
  assign RD3 = decoder_3_out6 ? R6_out : 8'bz;  // Controlled_Buffer controlled_buffer_17
  assign RD3 = decoder_3_out5 ? R5_out : 8'bz;  // Controlled_Buffer controlled_buffer_18
  assign RD3 = decoder_3_out4 ? R4_out : 8'bz;  // Controlled_Buffer controlled_buffer_19
  assign RD3 = decoder_3_out3 ? R3_out : 8'bz;  // Controlled_Buffer controlled_buffer_20
  assign RD3 = decoder_3_out2 ? R2_out : 8'bz;  // Controlled_Buffer controlled_buffer_21
  assign RD3 = decoder_3_out1 ? R1_out : 8'bz;  // Controlled_Buffer controlled_buffer_22
  assign RD3 = decoder_3_out0 ? R0_out : 8'bz;  // Controlled_Buffer controlled_buffer_23
  assign RD3 = decoder_3_out7 ? {8{1'b0}} : 8'bz;  // Controlled_Buffer controlled_buffer_24
  LedBar ledbar_4 (
    .led0(RD3[7]), .led1(RD3[6]), .led2(RD3[5]), .led3(RD3[4]), .led4(RD3[3]), .led5(RD3[2]), .led6(RD3[1]),
    .led7(RD3[0]));

  // Other names for the same wires on the sheet: EnWr = EnableWrite; R0[7:0] = R0_out; R1[7:0] = R1_out;
  //   R2[7:0] = R2_out; R3[7:0] = R3_out; R4[7:0] = R4_out; R5[7:0] = R5_out; R6[7:0] = R6_out
endmodule

module ALU (
  input  [4:0] AluOp,
  input  Enable,
  input  [7:0] RD1,
  input  [7:0] RD2,
  input  clk,
  output [7:0] Result
);

  wire adder_1_cout, ALU_A_Sign, ALU_B_Sign, ALU_Carry, ALU_Carry_IN, ALU_OverFlow, ALU_Zero, and_1_out,
       CondMatch, Flags_Carry, Flags_OutSign, Flags_Overflow, flags_swap, Flags_Zero, multiplexer_3_out,
       multiplexer_6_out, nor_1_out, nor_2_out, or_1_out, or_2_out, xor_1_out, xor_2_out, xor_3_out;
  wire [1:0] COp, SOp;
  wire [3:0] LOp, multiplexer_2_out;
  wire [6:0] multiplexer_1_out, pla_decoder_lop_1_result;
  wire [7:0] ALU, bit_extender_1_out;

  LedBar #(.matrixcols(5)) ledbar_1 (
    .led0(AluOp[4]), .led1(AluOp[3]), .led2(AluOp[2]), .led3(AluOp[1]), .led4(AluOp[0]));
  Multiplexer #(.select(2), .width(8)) multiplexer_1 (
    .in0({8{1'b0}}), .in1(RD1), .in2({RD1[6:0], ALU_Carry_IN}), .in3({ALU_Carry_IN, RD1[7:1]}),
    .out({ALU_A_Sign, multiplexer_1_out}), .sel(SOp));
  LedBar #(.matrixcols(2)) ledbar_2 (.led0(COp[1]), .led1(COp[0]));
  AluDecoder aludecoder_1 (.F(AluOp), .CondMatch(CondMatch), .COp(COp), .SOp(SOp), .InvRHS(LOp));
  LedBar #(.matrixcols(2)) ledbar_3 (.led0(SOp[1]), .led1(SOp[0]));
  PLA_Decoder_LOp pla_decoder_lop_1 (
    .LOp(LOp), .RD2(RD2[3:0]), .RD1(RD1[3:0]), .Swap(flags_swap), .result(pla_decoder_lop_1_result[3:0]));
  PLA_Decoder_LOp pla_decoder_lop_2 (
    .LOp(LOp), .RD2(RD2[7:4]), .RD1(RD1[7:4]), .result({ALU_B_Sign, pla_decoder_lop_1_result[6:4]}));  // open: Swap
  Multiplexer #(.width(4)) multiplexer_2 (
    .in0({ALU_OverFlow, ALU[7], ALU_Zero, ALU_Carry}), .in1(RD1[3:0]), .out(multiplexer_2_out),
    .sel(flags_swap));
  Register #(.width(4)) Flags (
    .D(multiplexer_2_out), .en(and_1_out), .clk(clk),
    .Q({Flags_Overflow, Flags_OutSign, Flags_Zero, Flags_Carry}));  // open: clr
  and and_1 (and_1_out, Enable, ~AluOp[4]);  // AND_Gate
  Multiplexer #(.select(2)) multiplexer_3 (
    .in0(ALU_Carry_IN), .in1(ALU_Carry_IN), .in2(1'b0), .in3(1'b0), .out(multiplexer_3_out), .sel(SOp));
  LedBar #(.matrixcols(4)) ledbar_4 (.led0(LOp[3]), .led1(LOp[2]), .led2(LOp[1]), .led3(LOp[0]));
  Adder adder_1 (
    .a({ALU_A_Sign, multiplexer_1_out}), .b({ALU_B_Sign, pla_decoder_lop_1_result}), .out(ALU),
    .cin(multiplexer_3_out), .cout(adder_1_cout));
  Multiplexer #(.select(2)) multiplexer_4 (
    .in0(adder_1_cout), .in1(adder_1_cout), .in2(RD1[7]), .in3(RD1[0]), .out(ALU_Carry), .sel(SOp));
  nor nor_1 (nor_1_out, ALU[0], ALU[1], ALU[2], ALU[3]);
  nor nor_2 (nor_2_out, ALU[4], ALU[5], ALU[6], ALU[7]);
  and and_2 (ALU_Zero, nor_1_out, nor_2_out);
  Multiplexer #(.select(2)) multiplexer_5 (
    .in0(1'b0), .in1(1'b1), .in2(Flags_Carry), .in3(Flags_Carry), .out(ALU_Carry_IN), .sel(COp));
  xor xor_1 (xor_1_out, ALU[7], ALU_A_Sign);
  xor xor_2 (xor_2_out, ALU[7], ALU_B_Sign);
  and and_3 (ALU_OverFlow, xor_1_out, xor_2_out);
  or or_1 (or_1_out, ~Flags_Carry, Flags_Zero);  // OR_Gate
  xor xor_3 (xor_3_out, Flags_OutSign, Flags_Overflow);
  or or_2 (or_2_out, xor_3_out, Flags_Zero);
  Multiplexer #(.select(3)) multiplexer_6 (
    .in0(1'b1), .in1(Flags_Carry), .in2(Flags_Zero), .in3(Flags_OutSign), .in4(Flags_Overflow),
    .in5(or_1_out), .in6(xor_3_out), .in7(or_2_out), .out(multiplexer_6_out), .sel(AluOp[3:1]));
  xor xor_4 (CondMatch, multiplexer_6_out, AluOp[0]);
  assign bit_extender_1_out = {{4{1'b0}}, {Flags_Overflow, Flags_OutSign, Flags_Zero, Flags_Carry}};  // Bit_Extender bit_extender_1
  Multiplexer #(.width(8)) multiplexer_7 (.in0(ALU), .in1(bit_extender_1_out), .out(Result), .sel(flags_swap));

  // Other names for the same wires on the sheet: ALU_Out_Sign = ALU[7];
  //   FlagsReg[3:0] = {Flags_Overflow, Flags_OutSign, Flags_Zero, Flags_Carry}; writeback_alu = Enable
endmodule

module ProgramCounter (
  input  [7:0] RelativeAddr,
  input  [15:0] AbisoluteAddr,
  input  [1:0] CounterMode,
  input  clk,
  input  Reset,
  output [15:0] PC
);

  wire [15:0] adder_1_out, adder_2_out, bit_extender_1_out, multiplexer_1_out;

  Adder #(.width(16)) adder_1 (.a(PC), .b(16'h2), .out(adder_1_out));  // open: cin, cout
  Adder #(.width(16)) adder_2 (.a(PC), .b(bit_extender_1_out), .out(adder_2_out));  // open: cin, cout
  assign bit_extender_1_out = {{8{RelativeAddr[7]}}, RelativeAddr};  // Bit_Extender bit_extender_1
  Register #(.width(16)) register_1 (.D(multiplexer_1_out), .clk(clk), .Q(PC), .clr(Reset));  // open: en
  Multiplexer #(.select(2), .width(16)) multiplexer_1 (
    .in0(adder_1_out), .in1(adder_2_out), .in2(AbisoluteAddr), .out(multiplexer_1_out), .sel(CounterMode));  // open: in3
endmodule

module RomData (
  input  [15:0] PC,
  input  clk,
  input  NotEnable,
  output [15:0] RomOut
);

  wire or_1_out;

  ROM #(.addrWidth(16)) rom_1 (.addr({PC[15:1], clk}), .data(RomOut[15:8]));
  Register #(.trigger("high")) register_1 (.D(RomOut[15:8]), .clk(clk), .Q(RomOut[7:0]));  // open: en, clr
  // NOT_Gate not_1 has open pins: in=or_1_out, out=open
  or or_1 (or_1_out, clk, NotEnable);

  // Other names for the same wires on the sheet: PcReg[15:0] = PC; en = NotEnable

  // Notes on the sheet:
  //   contents of rom_1 (hex, n*v repeats v):
  //   ff 41 ff 81 ff c1 ff 17 ff 57 0 97 0 d7 18 5f aa 41 18 5f 18 9e
endmodule

module bin_to_bcd (
  input  [7:0] in_1,
  output [3:0] bcd100,
  output [3:0] bcd10,
  output [3:0] bcd1
);

  PLA #(.in_width(8), .out_width(1), .\table ("1000000x 1\n1001010x 1\n1011001x 1\n0111001x 1\n1100001x 1\n1001001x 1\n1100011x 1\n10x1000x 1\n1000010x 1\n1000101x 1\n011010xx 1\n1001101x 1\n101110xx 1\n1000100x 1\n01110x0x 1\n10000x1x 1\n1001x11x 1\n11000x0x 1\n1011x1xx 1\n10x011xx 1\n10011x0x 1\n01111xxx 1\n011xx1xx 1\n1010xxxx 1")) pla_1 (
    .in(in_1), .out(bcd100[0]));
  PLA #(.in_width(8), .out_width(1), .\table ("1101000x 1\n1110010x 1\n1101010x 1\n111000xx 1\n11010x1x 1\n1110x11x 1\n1111xxxx 1\n11xx1xxx 1")) pla_2 (
    .in(in_1), .out(bcd100[1]));
  PLA #(.in_width(8), .out_width(1), .\table ("000100xx 1\n10011xxx 1\n0011101x 1\n0011100x 1\n0x0011xx 1\n010x11xx 1\n11x0011x 1\n011000xx 1\n0100x11x 1\n1001x11x 1\n110x0x1x 1\n1x1x111x 1\n110x01xx 1\nx011001x 1\n001101xx 1\n101100xx 1\nx110111x 1\n100001xx 1\n11111x1x 1\n1x000x1x 1\n100x10xx 1\n0x0x111x 1\n0x001x1x 1\n1x0110xx 1\n1x101x1x 1\n010x1x1x 1\n00100xxx 1\n1x1011xx 1\n01001xxx 1\n111x11xx 1\n11101xxx 1\n01110xxx 1\n11000xxx 1")) pla_3 (
    .in(in_1), .out(bcd10[0]));
  PLA #(.in_width(8), .out_width(1), .\table ("00011xxx 1\n110111xx 1\n101100xx 1\n100001xx 1\n0001x1xx 1\n0x1111xx 1\n01111xxx 1\n00100xxx 1\n10x0x0xx 1\n1110xxxx 1\n0100xxxx 1\n1010xxxx 1")) pla_4 (
    .in(in_1), .out(bcd10[1]));
  PLA #(.in_width(8), .out_width(1), .\table ("x011000x 1\nx011001x 1\n001101xx 1\n10x011xx 1\n001x1xxx 1\n1111xxxx 1\n0100xxxx 1\n1001xxxx 1\n1010xxxx 1")) pla_5 (
    .in(in_1), .out(bcd10[2]));
  PLA #(.in_width(8), .out_width(1), .\table ("1011101x 1\n1011100x 1\n011000xx 1\n1011x1xx 1\n11000xxx 1\n0101xxxx 1")) pla_6 (
    .in(in_1), .out(bcd10[3]));
  PLA #(.in_width(8), .out_width(1), .\table ("xxxxxxx1 1")) pla_7 (.in(in_1), .out(bcd1[0]));
  PLA #(.in_width(8), .out_width(1), .\table ("0001101x 1\n1011101x 1\n0110011x 1\n1x00111x 1\n110x111x 1\n010x110x 1\n1011000x 1\n1x10110x 1\n1101010x 1\n010x001x 1\n0001000x 1\n0011010x 1\n111x001x 1\n0110000x 1\n00000x1x 1\n011x101x 1\n0011100x 1\n0x01011x 1\n10100x1x 1\n1001001x 1\n1101100x 1\n1x11011x 1\n00101x1x 1\n0x11111x 1\n11001x1x 1\n1000010x 1\n0x00110x 1\n111x110x 1\n1000100x 1\n00100x0x 1\n01110x0x 1\n11000x0x 1\n11101x0x 1\n01001x0x 1\n10011x0x 1")) pla_8 (
    .in(in_1), .out(bcd1[1]));
  PLA #(.in_width(8), .out_width(1), .\table ("1100x10x 1\n1001110x 1\n11x0110x 1\nx101011x 1\n00x0111x 1\n01x1111x 1\n110011xx 1\n1110x01x 1\n0100x01x 1\n0001000x 1\n0010x10x 1\n0010001x 1\n0111001x 1\n0110000x 1\n0111x10x 1\n000001xx 1\nx100110x 1\n0011100x 1\n10x0011x 1\n010101xx 1\n101001xx 1\n0011011x 1\n1100001x 1\n1001001x 1\n1101100x 1\n111101xx 1\nx010111x 1\n10x1000x 1\nx111111x 1\n011010xx 1\n000110xx 1\n111000xx 1\n1001101x 1\n010000xx 1\n101110xx 1\n1000100x 1")) pla_9 (
    .in(in_1), .out(bcd1[2]));
  PLA #(.in_width(8), .out_width(1), .\table ("0000100x 1\n0101100x 1\n1010100x 1\n1101000x 1\n0011000x 1\n1111100x 1\n0001110x 1\n0110110x 1\n1011110x 1\n0100111x 1\n1001111x 1\n1110111x 1\n1000000x 1\n1110010x 1\n0001001x 1\n0100010x 1\n1001010x 1\n0110001x 1\n1011001x 1\n0011101x 1\n1101101x 1\n0111011x 1\n0010011x 1\n1100011x 1\n1000101x 1")) pla_10 (
    .in(in_1), .out(bcd1[3]));

  assign bcd100[3:2] = 2'b00;
endmodule

module bcd_7seg (
  input  [3:0] bcd,
  output a,
  output b,
  output c,
  output d,
  output e,
  output f,
  output g,
  output decimal
);

  wire and_1_out, and_2_out, and_3_out, and_4_out, and_5_out, and_6_out, and_7_out, and_8_out, and_9_out,
       and_10_out, and_11_out, and_12_out, and_13_out, and_14_out, and_15_out, and_16_out, and_17_out,
       and_18_out, and_19_out, not_1_out, not_2_out, not_3_out;

  not not_1 (not_1_out, bcd[2]);
  not not_2 (not_2_out, bcd[1]);
  not not_3 (not_3_out, bcd[0]);
  and and_1 (and_1_out, not_1_out, not_3_out);
  and and_2 (and_2_out, bcd[2], bcd[0]);
  and and_3 (and_3_out, not_1_out, bcd[1]);
  and and_4 (and_4_out, not_2_out, not_3_out);
  and and_5 (and_5_out, bcd[1], bcd[0]);
  or or_1 (c, not_2_out, bcd[0], bcd[2]);
  and and_6 (and_6_out, not_1_out, not_3_out);
  and and_7 (and_7_out, not_1_out, bcd[1]);
  and and_8 (and_8_out, bcd[2], not_2_out, bcd[0]);
  and and_9 (and_9_out, bcd[1], not_3_out);
  and and_10 (and_10_out, not_1_out, not_3_out);
  and and_11 (and_11_out, bcd[1], not_3_out);
  and and_12 (and_12_out, not_2_out, not_3_out);
  and and_13 (and_13_out, bcd[2], not_2_out);
  and and_14 (and_14_out, bcd[2], not_3_out);
  and and_15 (and_15_out, not_1_out, bcd[1]);
  and and_16 (and_16_out, bcd[2], not_2_out);
  and and_17 (and_17_out, bcd[1], not_3_out);
  and and_18 (and_18_out, bcd[2], bcd[1], not_3_out);
  and and_19 (and_19_out, bcd[3], bcd[0]);
  or or_2 (a, and_1_out, and_2_out, bcd[3], and_3_out);
  or or_3 (b, not_1_out, and_4_out, and_5_out);
  or or_4 (d, and_6_out, and_7_out, and_8_out, and_9_out);
  or or_5 (e, and_10_out, and_11_out);
  or or_6 (f, and_12_out, and_13_out, and_14_out, bcd[3]);
  or or_7 (g, and_15_out, and_16_out, bcd[3], and_17_out);
  or or_8 (decimal, and_18_out, and_19_out);
endmodule

module InstructionDecoder (
  input  [5:0] opcode,
  output [1:0] CounterMode,
  output writeback_alu,
  output op2_is_imm,
  output en_write_reg1,
  output small_rd,
  output [1:0] LdiCode,
  output Ram_out,
  output Ram_In,
  output [4:0] AluOp
);

  wire and_2_out, and_3_out, and_4_out, and_5_out, and_6_out, and_7_out, and_8_out, and_9_out, and_10_out,
       and_11_out, and_12_out, and_13_out, and_14_out, and_15_out, and_16_out, and_17_out, and_18_out,
       and_19_out, and_24_out, and_25_out, and_26_out, and_27_out, and_28_out, and_29_out, and_30_out,
       and_31_out, and_32_out, and_33_out, and_34_out, and_35_out, and_36_out, and_37_out, not_1_out,
       not_2_out, not_3_out, not_4_out, not_5_out, not_6_out;

  not not_1 (not_1_out, opcode[5]);
  not not_2 (not_2_out, opcode[4]);
  not not_3 (not_3_out, opcode[3]);
  not not_4 (not_4_out, opcode[2]);
  not not_5 (not_5_out, opcode[1]);
  not not_6 (not_6_out, opcode[0]);
  and and_1 (CounterMode[1], not_1_out, not_2_out, not_3_out, opcode[2], not_5_out, opcode[0]);
  and and_2 (and_2_out, not_1_out, not_2_out, not_3_out, not_4_out, opcode[1], opcode[0]);
  and and_3 (and_3_out, not_1_out, not_2_out, not_3_out, opcode[2], not_5_out, not_6_out);
  and and_4 (and_4_out, not_2_out, opcode[2], opcode[1]);
  and and_5 (and_5_out, not_2_out, opcode[3]);
  and and_6 (and_6_out, opcode[4], not_3_out, not_4_out);
  and and_7 (and_7_out, opcode[4], not_3_out, not_5_out);
  and and_8 (and_8_out, opcode[4], not_3_out, not_6_out);
  and and_9 (and_9_out, not_3_out, opcode[0]);
  and and_10 (and_10_out, not_4_out, not_5_out);
  and and_11 (and_11_out, opcode[3], not_6_out);
  and and_12 (and_12_out, not_4_out, not_5_out, opcode[0]);
  and and_13 (and_13_out, opcode[1], not_6_out);
  and and_14 (and_14_out, opcode[4], not_4_out);
  and and_15 (and_15_out, not_2_out, opcode[3]);
  and and_16 (and_16_out, not_3_out, opcode[2], opcode[1]);
  and and_17 (and_17_out, opcode[4], not_3_out, opcode[2], opcode[1], opcode[0]);
  and and_18 (and_18_out, not_1_out, not_2_out, not_3_out, not_4_out, opcode[0]);
  and and_19 (and_19_out, opcode[4], opcode[3], not_4_out);
  and and_20 (LdiCode[1], opcode[4], not_4_out);
  and and_21 (LdiCode[0], opcode[4], opcode[0]);
  and and_22 (Ram_out, opcode[4], opcode[3], opcode[1], not_6_out);
  and and_23 (Ram_In, opcode[4], opcode[3], opcode[1], opcode[0]);
  and and_24 (and_24_out, opcode[5], opcode[3]);
  and and_25 (and_25_out, opcode[3], opcode[2], opcode[1]);
  and and_26 (and_26_out, opcode[4], opcode[1]);
  and and_27 (and_27_out, not_1_out, not_3_out, not_4_out);
  and and_28 (and_28_out, not_1_out, not_3_out, not_5_out, opcode[0]);
  and and_29 (and_29_out, opcode[5], opcode[2]);
  and and_30 (and_30_out, not_1_out, not_4_out, opcode[1]);
  and and_31 (and_31_out, opcode[4], opcode[1]);
  and and_32 (and_32_out, not_2_out, opcode[2], not_5_out);
  and and_33 (and_33_out, not_1_out, not_3_out, not_5_out, opcode[0]);
  and and_34 (and_34_out, opcode[5], opcode[1]);
  and and_35 (and_35_out, not_1_out, not_5_out, not_6_out);
  and and_36 (and_36_out, not_1_out, not_2_out, not_5_out);
  and and_37 (and_37_out, not_3_out, not_4_out, opcode[1]);
  or or_1 (CounterMode[0], and_2_out, and_3_out);
  or or_2 (writeback_alu, and_4_out, and_5_out, opcode[5], and_6_out, and_7_out, and_8_out);
  or or_3 (op2_is_imm, and_9_out, and_10_out, and_11_out);
  or or_4 (en_write_reg1, and_12_out, and_13_out, and_14_out, opcode[5], and_15_out, and_16_out);
  or or_5 (small_rd, and_17_out, and_18_out, and_19_out);
  or or_6 (AluOp[3], and_24_out, and_25_out, and_26_out, and_27_out, and_28_out);
  or or_7 (AluOp[2], and_29_out, and_30_out, and_31_out, and_32_out, and_33_out);
  or or_8 (AluOp[1], and_34_out, and_35_out, and_36_out, and_37_out);

  assign {AluOp[4], AluOp[0]} = {opcode[5], opcode[0]};
endmodule
