// Logisim project temp.circ as structural Verilog: 1 circuit, main circuit sop
module sop (
  input  [2:0] A,
  input  [1:0] B,
  output [2:0] S
);

  wire _t0, _t1, _t2, _t3, _t4, _t5, _t6, _t7, _t8, _t9, _t10, _t11, _t12, _t13, _t14, _t15, A0_n, A1_n,
       A2_n, and_2_out, and_4_out, and_5_out, and_7_out, and_8_out, and_10_out, and_12_out, and_13_out,
       and_15_out, and_17_out, and_19_out, and_20_out, and_22_out, and_23_out, and_25_out, and_27_out,
       and_29_out, and_31_out, and_33_out, B0_n, B1_n, or_1_out, or_2_out, or_3_out, or_4_out, or_5_out,
       or_6_out, or_7_out, or_8_out, or_9_out, or_10_out;

  not not_1 (A2_n, A[2]);
  not not_2 (A1_n, A[1]);
  not not_3 (A0_n, A[0]);
  not not_4 (B1_n, B[1]);
  not not_5 (B0_n, B[0]);
  and and_1 (_t0, A[2], and_2_out);
  and and_2 (and_2_out, A1_n, B0_n);
  and and_3 (_t1, A[2], and_4_out);
  and and_4 (and_4_out, A0_n, B1_n);
  and and_5 (and_5_out, A2_n, A[1]);
  and and_6 (_t2, and_5_out, and_7_out);
  and and_7 (and_7_out, A[0], B[0]);
  and and_8 (and_8_out, A2_n, A[0]);
  and and_9 (_t3, and_8_out, and_10_out);
  and and_10 (and_10_out, B[1], B[0]);
  and and_11 (_t4, A[2], and_12_out);
  and and_12 (and_12_out, A1_n, A0_n);
  and and_13 (and_13_out, A[2], A1_n);
  and and_14 (_t5, and_13_out, and_15_out);
  and and_15 (and_15_out, B1_n, B[0]);
  and and_16 (_t6, A[2], and_17_out);
  and and_17 (and_17_out, B1_n, B0_n);
  and and_18 (_t7, A2_n, and_19_out);
  and and_19 (and_19_out, A[1], B[1]);
  and and_20 (and_20_out, A1_n, A[0]);
  and and_21 (_t8, and_20_out, and_22_out);
  and and_22 (and_22_out, B1_n, B[0]);
  and and_23 (and_23_out, A[1], A[0]);
  and and_24 (_t9, and_23_out, and_25_out);
  and and_25 (and_25_out, B[1], B[0]);
  and and_26 (_t10, A[1], and_27_out);
  and and_27 (and_27_out, B1_n, B0_n);
  and and_28 (_t11, A[1], and_29_out);
  and and_29 (and_29_out, A0_n, B1_n);
  and and_30 (_t12, A1_n, and_31_out);
  and and_31 (and_31_out, B[1], B0_n);
  and and_32 (_t13, A1_n, and_33_out);
  and and_33 (and_33_out, A0_n, B[1]);
  and and_34 (_t14, A[0], B0_n);
  and and_35 (_t15, A0_n, B[0]);
  or or_1 (or_1_out, _t0, _t1);
  or or_2 (or_2_out, _t2, _t3);
  or or_3 (or_3_out, _t4, _t5);
  or or_4 (or_4_out, _t6, _t7);
  or or_5 (or_5_out, _t9, _t10);
  or or_6 (or_6_out, _t12, _t13);
  or or_7 (or_7_out, or_1_out, or_2_out);
  or or_8 (or_8_out, or_3_out, or_4_out);
  or or_9 (or_9_out, _t8, or_5_out);
  or or_10 (or_10_out, _t11, or_6_out);
  or or_11 (S[2], or_7_out, or_8_out);
  or or_12 (S[1], or_9_out, or_10_out);
  or or_13 (S[0], _t14, _t15);

  // Other names for the same wires on the sheet: _go_S0 = S[0]; _go_S1 = S[1]; _go_S2 = S[2]
endmodule
